# Fritzing sketch FanControl_IOT_v3-3 (saved by Fritzing 0.9.4)
circuit board: 8.46667cm x 5.64444cm
breadboards: 3

parts:
  IC1 = ProMicro (ATMega32U4)
  DHT1 = Humidity and Temperature Sensor DHT11
  DHT2 = Humidity and Temperature Sensor DHT11
  LCD1 = LCD screen
  PW1 = Power plug
  VREG1 = Voltage Regulator - 5V [package="TO220 [THT]"]
  J1 = male pin header, 4 pins [form="♂ (male)"]
  BT4 = Momentary Switch [package=ksa_sealed_tac_switch]
  BT3 = Momentary Switch [package=ksa_sealed_tac_switch]
  BT2 = Momentary Switch [package=ksa_sealed_tac_switch]
  BT1 = Momentary Switch [package=ksa_sealed_tac_switch]
  RLY1 = RELAY [package=relay-jzc]
  RV1 = Trimmer Potentiometer [maximum_resistance=10kΩ package=THT]
  D1 = Rectifier Diode [part_number=1N4001 package="300 mil [THT]"]
  IC2 = Arduino Nano (Rev3.0)
  LL1 = mystery part, 12 pins [chip_label="Logic level converter"]
  DIP2 = mystery part, 20 pins [chip_label="LCD I2C Converter"]
  RH2 = Resistor [tolerance=±5% resistance=1k package=THT]
  RH3 = Resistor [tolerance=±5% resistance=1k package=THT]
  RH4 = Resistor [tolerance=±5% resistance=1k package=THT]
  RH1 = Resistor [tolerance=±5% resistance=1k package=THT]
  RH5 = Resistor [tolerance=±5% resistance=1k package=THT]
  J2 = male pin header, 4 pins [form="♂ (male)"]
  RLY2 = RELAY [package=relay-jzc]

nets:
  N1: IC1.D1_/_TXD1, LL1.pin12
  N2: IC1.D0_/_RXD1, LL1.pin11
  GND: IC1.GND, DHT1.GND, DHT2.GND, LCD1.VSS, PW1.GND, VREG1.GND, J1.pin4, RLY1.COIL2, RV1.leg2, IC2.GND, LL1.pin4, LL1.pin9, DIP2.pin20, RH5.Pin_1, J2.pin4, RLY2.COIL2
  N3: IC1.D2_/_SDA, J2.pin2
  N4: IC1.D3_PWM_/_SCL, J1.pin2
  N5: IC1.D6_PWM_/_A7, J1.pin1, J2.pin1
  N6: IC1.D14_/_MISO, RLY2.COIL1
  N7: IC1.D15_/_SCK, RLY1.COIL1
  N8: IC1.D20_/_A2, DHT2.Data-signal
  N9: IC1.D21_/_A3, DHT1.Data-signal
  VCC: IC1.VCC, DHT1.Vcc, DHT2.Vcc, LCD1.VDD, RV1.leg1, D1.anode, IC2.VIN, LL1.pin10, RH1.Pin_0
  N10: LCD1.V0, RV1.wiper
  N11: LCD1.RS, DIP2.pin18
  N12: LCD1.R/W, DIP2.pin17
  N13: LCD1.E, DIP2.pin16
  N14: LCD1.DB0, DIP2.pin1
  N15: LCD1.DB1, DIP2.pin2
  N16: LCD1.DB2, DIP2.pin3
  N17: LCD1.DB3, DIP2.pin4
  N18: LCD1.DB4, DIP2.pin5
  N19: LCD1.DB5, DIP2.pin6
  N20: LCD1.DB6, DIP2.pin7
  N21: LCD1.DB7, DIP2.pin8
  N22: LCD1.LED+, DIP2.pin9
  N23: LCD1.LED-, DIP2.pin10
  N24: PW1.VCC, VREG1.input_voltage, RLY1.MAIN, RLY2.MAIN
  N25: VREG1.output_voltage, D1.cathode
  N26: J1.pin3, RLY1.NO
  N27: BT4.1, BT3.1, BT2.1, BT1.1, IC2.A1
  N28: BT4.3, RH4.Pin_1, RH5.Pin_0
  N29: BT3.3, RH3.Pin_1, RH4.Pin_0
  N30: BT2.3, RH2.Pin_1, RH3.Pin_0
  N31: BT1.3, RH2.Pin_0, RH1.Pin_1
  N32: IC2.D1/TX, LL1.pin2
  N33: IC2.D0/RX, LL1.pin1
  N34: IC2.A5, LL1.pin6
  N35: IC2.A4, LL1.pin5
  N36: IC2.3V3, LL1.pin3
  N37: LL1.pin7, DIP2.pin11
  N38: LL1.pin8, DIP2.pin12
  N39: J2.pin3, RLY2.NO

custom parts:
  ProMicro (ATMega32U4): The ProMicro is a microcontroller board based on the ATmega32u4 (datasheet), developed in conjunction with Adafruit. It has 18 digital input/output pins (of which 5 can be used as PWM outputs and 9 as analog inputs), a 16 MHz crystal oscillator and micro USB connection. It contains everything needed to support the microcontroller; simply connect it to a computer with a micro USB cable to get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
  Humidity and Temperature Sensor DHT11: Digital relative humidity & temperature sensor DHT11
